# Fritzing sketch digital_in (saved by Fritzing 0.7.0b)
breadboards: 1

parts:
  S1 = Pushbutton [package="[THT]"]
  U1 = Arduino Mega

nets:
  N1: S1.Pin_1, S1.Pin_2, U1.A6
  N2: S1.Pin_3, S1.Pin_4, U1.GND
